# Fritzing sketch layout (saved by Fritzing 0.9.3b)
circuit board: 7cm x 10cm
breadboards: 1

parts:
  LEFT = SWITCH-MOMENTARY-2 [package=tactile-pth-12mm]
  UP = SWITCH-MOMENTARY-2 [package=tactile-pth-12mm]
  RIGHT = SWITCH-MOMENTARY-2 [package=tactile-pth-12mm]
  DOWN = SWITCH-MOMENTARY-2 [package=tactile-pth-12mm]
  B = SWITCH-MOMENTARY-2 [package=tactile-pth-12mm]
  A = SWITCH-MOMENTARY-2 [package=tactile-pth-12mm]
  DISPLAY = SH1106 [form="♀ (female)" package=THT]  # not connected
  STM32 = STM32F103 [package="LQFP64, 10x10mm"]

nets:
  N1: LEFT.1, STM32.PB3
  GND: LEFT.2, UP.2, RIGHT.2, DOWN.2, B.2, A.2
  N2: UP.1, STM32.PB5
  N3: RIGHT.1, STM32.PB8
  N4: DOWN.1, STM32.PB4
  N5: B.1, STM32.PB6
  N6: A.1, STM32.PB7

custom parts:
  STM32F103: STM32F403xx microcontroller in LQFP64 pinout
